# Fritzing sketch ProgettoSensori (saved by Fritzing 0.9.3b)
breadboards: 2

parts:
  J1 = STM32 Nucleo boards
  C1 = Electrolytic Capacitor [capacitance=1000μF package="1010 [SMD, electrolytic]"]
  C2 = Electrolytic Capacitor [capacitance=1000μF package="1010 [SMD, electrolytic]"]
  J2 = STM32 Nucleo boards
  R1 = Resistor [tolerance=±5% resistance=220 package="2512 [SMD]"]
  R2 = Resistor [tolerance=±5% resistance=220 package="2512 [SMD]"]
  Raspberry_Pi_1 = Raspberry Pi 3 [part_number=RPI-3-V1.2]
  U2 = LCD-16X2 [package=lcd-16x2_noholes]
  R3 = Rotary Potentiometer (Small) [maximum_resistance=100kΩ package=THT]
  R4 = Resistor [tolerance=±5% resistance=220 package="2512 [SMD]"]

nets:
  N1: J1.D12/MISO, R2.Pin_1
  N2: J1.GND, J2.GND#1189
  N3: J1.D7, R1.Pin_1
  N4: C1.-, C2.-, J2.GND#1188
  N5: C1.+, J2.A1, R1.Pin_0
  N6: C2.+, J2.A0, R2.Pin_0
  N7: J2.D8, Raspberry_Pi_1.GPIO6
  N8: J2.D13/SCK, Raspberry_Pi_1.GND, U2.DB4
  N9: J2.GND#1157, Raspberry_Pi_1.GPIO19
  N10: J2.D2, Raspberry_Pi_1.GPIO13
  N11: Raspberry_Pi_1.GPIO26, U2.VDD, R4.Pin_1
  N12: Raspberry_Pi_1.GPIO24, U2.E
  N13: Raspberry_Pi_1.GPIO18, U2.DB7
  N14: Raspberry_Pi_1.GPIO15, U2.DB6
  N15: Raspberry_Pi_1.GPIO14, U2.DB5
  5V: Raspberry_Pi_1.5V, U2.VSS, U2.RS, U2.R_W, U2.K, R3.leg1
  N16: U2.VO, R3.wiper
  N17: U2.A, R4.Pin_0
